# Fritzing sketch IRsensorCircuit (saved by Fritzing 0.9.3b)
breadboards: 1

parts:
  R1 = Resistor [tolerance=±5% resistance=200 package=THT]
  Q1 = PHOTOTRANSISTOR REFLECTIVE OBJECT SENSOR [package=qrb1114-side]
  Part1 = Arduino Uno (Rev3)
  R2 = Resistor [tolerance=±5% resistance=10k package=THT]
  Q2 = PHOTOTRANSISTOR REFLECTIVE OBJECT SENSOR [package=qrb1114-side]
  R4 = Resistor [tolerance=±1% resistance=10k package=THT]
  R3 = Resistor [tolerance=±5% resistance=200 package=THT]

nets:
  N1: R1.Pin_0, Q1.A
  N2: R1.Pin_1, Part1.5V, R2.Pin_0, R4.Pin_0, R3.Pin_1
  N3: Q1.C, Part1.A0, R2.Pin_1
  N4: Q1.E, Q1.K, Part1.GND, Q2.E, Q2.K
  N5: Part1.A2, Q2.C, R4.Pin_1
  N6: Q2.A, R3.Pin_0
